// Logisim project 32bit-MicrocodedCPU.circ as structural Verilog: 6 circuits, main circuit main
// address
module main (
  input  reset
);

  wire c, clock_1_out, clock_2_out, datawrite, dwrite, imload, irload, n, not_1_out, pcload, swrite, z;
  wire [1:0] addrsel, datasel, op2sel, pcsel, regsrc;
  wire [3:0] aluop;
  wire [4:0] irlogic_1_dsel, irlogic_1_ssel, irlogic_1_tsel;
  wire [7:0] Microcode_Logic_ucounter, opcode;
  wire [23:0] multiplexer_1_out;
  wire [31:0] aluout, dreg, immed, multiplexer_2_out, multiplexer_3_out, multiplexer_4_out, pc, ram_1_data,
       sreg, treg;
  wire [31:24] multiplexer_1_out_2;

  // Probe on multiplexer_1_out
  // Probe on Microcode_Logic_ucounter
  // Probe on c
  ucodelogic Microcode_Logic (
    .n(n), .z(z), .opcode(opcode[6:0]), .aluop(aluop), .op2sel(op2sel), .datawrite(datawrite),
    .addrsel(addrsel), .pcsel(pcsel), .pcload(pcload), .dwrite(dwrite), .irload(irload), .imload(imload),
    .regsrc(regsrc), .ucounter(Microcode_Logic_ucounter), .datasel(datasel), .swrite(swrite), .c(c));
  // Probe on z
  // Probe on n
  // Probe on opcode[6:0]
  // Probe on {multiplexer_1_out_2, multiplexer_1_out}
  // Probe on aluop
  // Probe on op2sel
  // Probe on datawrite
  // Probe on addrsel
  // Probe on pcsel
  // Probe on pcload
  // Probe on dwrite
  // Probe on irload
  // Probe on imload
  // Probe on regsrc
  // Probe on datasel
  // Probe on swrite
  Multiplexer #(.select(2), .width(32)) multiplexer_1 (
    .in0(pc), .in1(immed), .in2(aluout), .in3(sreg), .out({multiplexer_1_out_2, multiplexer_1_out}),
    .sel(addrsel));  // open: en
  // Probe on ram_1_data
  not not_1 (not_1_out, datawrite);
  Clock clock_1 (.out(clock_1_out));
  RAM #(.addrWidth(24), .dataWidth(32)) ram_1 (
    .addr(multiplexer_1_out), .data(ram_1_data), .clk(clock_1_out), .ld(not_1_out));  // open: sel, clr
  assign ram_1_data = datawrite ? multiplexer_2_out : 32'bz;  // Controlled_Buffer controlled_buffer_1
  Multiplexer #(.select(2), .width(32)) multiplexer_2 (
    .in0(pc), .in1(dreg), .in2(treg), .in3(aluout), .out(multiplexer_2_out), .sel(datasel));  // open: en
  // Probe on pc
  Register #(.width(32)) u_Immed (.D(ram_1_data), .en(imload), .Q(immed), .clk(clock_2_out));  // open: clr
  Clock clock_2 (.out(clock_2_out));
  pclogic pclogic_1 (.imreg(immed), .sreg(sreg), .pcout(pc), .pcsel(pcsel), .pcload(pcload), .reset(reset));
  Multiplexer #(.select(2), .width(32)) multiplexer_3 (
    .in0(ram_1_data), .in1(immed), .in2(aluout), .in3(sreg), .out(multiplexer_3_out), .sel(regsrc));  // open: en
  irlogic irlogic_1 (
    .irload(irload), .dsel(irlogic_1_dsel), .ssel(irlogic_1_ssel), .tsel(irlogic_1_tsel), .opcode(opcode),
    .instruction(ram_1_data));
  registerfile registerfile_1 (
    .regval(multiplexer_3_out), .dwrite(dwrite), .swrite(swrite), .dreg(dreg), .sreg(sreg), .treg(treg),
    .tsel(irlogic_1_tsel), .ssel(irlogic_1_ssel), .dsel(irlogic_1_dsel));  // open: twrite
  // Probe on irlogic_1_dsel
  // Probe on irlogic_1_ssel
  // Probe on irlogic_1_tsel
  // Probe on opcode
  Multiplexer #(.select(2), .width(32)) multiplexer_4 (
    .in0(treg), .in1(immed), .in2({32{1'b0}}), .in3(32'h1), .out(multiplexer_4_out), .sel(op2sel));  // open: en
  ALU alu_1 (.Negative(n), .Result(aluout), .aluop(aluop), .A(sreg), .B(multiplexer_4_out), .Carry(c), .Zero(z));
  // Probe on aluout
  // Probe on aluop
endmodule

// IR
module irlogic (
  input  [31:0] instruction,
  input  irload,
  output [4:0] dsel,
  output [4:0] ssel,
  output [4:0] tsel,
  output [7:0] opcode
);

  wire clock_1_out;
  wire [31:15] IR_q;

  Clock clock_1 (.out(clock_1_out));
  Register #(.width(32)) IR (
    .D(instruction), .en(irload), .Q({IR_q[31:24], opcode, IR_q[15], tsel, ssel, dsel}), .clk(clock_1_out));  // open: clr

  // Notes on the sheet:
  //   IR Logic
endmodule

// Regs
module registerfile (
  input  [31:0] regval,
  input  dwrite,
  input  swrite,
  input  twrite,
  input  [4:0] dsel,
  input  [4:0] ssel,
  input  [4:0] tsel,
  output [31:0] dreg,
  output [31:0] sreg,
  output [31:0] treg
);

  wire clock_1_out, demultiplexer_1_out0, demultiplexer_1_out1, demultiplexer_1_out2, demultiplexer_1_out3,
       demultiplexer_1_out4, demultiplexer_1_out5, demultiplexer_1_out6, demultiplexer_1_out7,
       demultiplexer_1_out8, demultiplexer_1_out9, demultiplexer_1_out10, demultiplexer_1_out11,
       demultiplexer_1_out12, demultiplexer_1_out13, demultiplexer_1_out14, demultiplexer_1_out15,
       demultiplexer_1_out16, demultiplexer_1_out17, demultiplexer_1_out18, demultiplexer_1_out19,
       demultiplexer_1_out20, demultiplexer_1_out21, demultiplexer_1_out22, demultiplexer_1_out23,
       demultiplexer_1_out24, demultiplexer_1_out25, demultiplexer_1_out26, demultiplexer_1_out27,
       demultiplexer_1_out28, demultiplexer_1_out29, demultiplexer_1_out30, demultiplexer_1_out31;
  wire [31:0] register_1_q, register_2_q, register_3_q, register_4_q, register_5_q, register_6_q,
       register_7_q, register_8_q, register_9_q, register_10_q, register_11_q, register_12_q, register_13_q,
       register_14_q, register_15_q, register_16_q, register_17_q, register_18_q, register_19_q,
       register_20_q, register_21_q, register_22_q, register_23_q, register_24_q, register_25_q,
       register_26_q, register_27_q, register_28_q, register_29_q, register_30_q, register_31_q,
       register_32_q;

  Demultiplexer #(.select(5)) demultiplexer_1 (
    .out0(demultiplexer_1_out0), .out1(demultiplexer_1_out1), .out2(demultiplexer_1_out2),
    .out3(demultiplexer_1_out3), .out4(demultiplexer_1_out4), .out5(demultiplexer_1_out5),
    .out6(demultiplexer_1_out6), .out7(demultiplexer_1_out7), .out8(demultiplexer_1_out8),
    .out9(demultiplexer_1_out9), .out10(demultiplexer_1_out10), .out11(demultiplexer_1_out11),
    .out12(demultiplexer_1_out12), .out13(demultiplexer_1_out13), .out14(demultiplexer_1_out14),
    .out15(demultiplexer_1_out15), .out16(demultiplexer_1_out16), .out17(demultiplexer_1_out17),
    .out18(demultiplexer_1_out18), .out19(demultiplexer_1_out19), .out20(demultiplexer_1_out20),
    .out21(demultiplexer_1_out21), .out22(demultiplexer_1_out22), .out23(demultiplexer_1_out23),
    .out24(demultiplexer_1_out24), .out25(demultiplexer_1_out25), .out26(demultiplexer_1_out26),
    .out27(demultiplexer_1_out27), .out28(demultiplexer_1_out28), .out29(demultiplexer_1_out29),
    .out30(demultiplexer_1_out30), .out31(demultiplexer_1_out31), .in(dwrite), .sel(dsel));  // open: en
  Demultiplexer #(.select(5)) demultiplexer_2 (
    .out0(demultiplexer_1_out0), .out1(demultiplexer_1_out1), .out2(demultiplexer_1_out2),
    .out3(demultiplexer_1_out3), .out4(demultiplexer_1_out4), .out5(demultiplexer_1_out5),
    .out6(demultiplexer_1_out6), .out7(demultiplexer_1_out7), .out8(demultiplexer_1_out8),
    .out9(demultiplexer_1_out9), .out10(demultiplexer_1_out10), .out11(demultiplexer_1_out11),
    .out12(demultiplexer_1_out12), .out13(demultiplexer_1_out13), .out14(demultiplexer_1_out14),
    .out15(demultiplexer_1_out15), .out16(demultiplexer_1_out16), .out17(demultiplexer_1_out17),
    .out18(demultiplexer_1_out18), .out19(demultiplexer_1_out19), .out20(demultiplexer_1_out20),
    .out21(demultiplexer_1_out21), .out22(demultiplexer_1_out22), .out23(demultiplexer_1_out23),
    .out24(demultiplexer_1_out24), .out25(demultiplexer_1_out25), .out26(demultiplexer_1_out26),
    .out27(demultiplexer_1_out27), .out28(demultiplexer_1_out28), .out29(demultiplexer_1_out29),
    .out30(demultiplexer_1_out30), .out31(demultiplexer_1_out31), .in(swrite), .sel(ssel));  // open: en
  Demultiplexer #(.select(5)) demultiplexer_3 (
    .out0(demultiplexer_1_out0), .out1(demultiplexer_1_out1), .out2(demultiplexer_1_out2),
    .out3(demultiplexer_1_out3), .out4(demultiplexer_1_out4), .out5(demultiplexer_1_out5),
    .out6(demultiplexer_1_out6), .out7(demultiplexer_1_out7), .out8(demultiplexer_1_out8),
    .out9(demultiplexer_1_out9), .out10(demultiplexer_1_out10), .out11(demultiplexer_1_out11),
    .out12(demultiplexer_1_out12), .out13(demultiplexer_1_out13), .out14(demultiplexer_1_out14),
    .out15(demultiplexer_1_out15), .out16(demultiplexer_1_out16), .out17(demultiplexer_1_out17),
    .out18(demultiplexer_1_out18), .out19(demultiplexer_1_out19), .out20(demultiplexer_1_out20),
    .out21(demultiplexer_1_out21), .out22(demultiplexer_1_out22), .out23(demultiplexer_1_out23),
    .out24(demultiplexer_1_out24), .out25(demultiplexer_1_out25), .out26(demultiplexer_1_out26),
    .out27(demultiplexer_1_out27), .out28(demultiplexer_1_out28), .out29(demultiplexer_1_out29),
    .out30(demultiplexer_1_out30), .out31(demultiplexer_1_out31), .in(twrite), .sel(tsel));  // open: en
  Register #(.width(32)) register_1 (
    .D(regval), .en(demultiplexer_1_out0), .Q(register_1_q), .clk(clock_1_out));  // open: clr
  Register #(.width(32)) register_2 (
    .D(regval), .en(demultiplexer_1_out1), .Q(register_2_q), .clk(clock_1_out));  // open: clr
  Register #(.width(32)) register_3 (
    .D(regval), .en(demultiplexer_1_out2), .Q(register_3_q), .clk(clock_1_out));  // open: clr
  Register #(.width(32)) register_4 (
    .D(regval), .en(demultiplexer_1_out3), .Q(register_4_q), .clk(clock_1_out));  // open: clr
  Register #(.width(32)) register_5 (
    .D(regval), .en(demultiplexer_1_out4), .Q(register_5_q), .clk(clock_1_out));  // open: clr
  Register #(.width(32)) register_6 (
    .D(regval), .en(demultiplexer_1_out5), .Q(register_6_q), .clk(clock_1_out));  // open: clr
  Register #(.width(32)) register_7 (
    .D(regval), .en(demultiplexer_1_out6), .Q(register_7_q), .clk(clock_1_out));  // open: clr
  Register #(.width(32)) register_8 (
    .D(regval), .en(demultiplexer_1_out7), .Q(register_8_q), .clk(clock_1_out));  // open: clr
  Register #(.width(32)) register_9 (
    .D(regval), .en(demultiplexer_1_out8), .Q(register_9_q), .clk(clock_1_out));  // open: clr
  Register #(.width(32)) register_10 (
    .D(regval), .en(demultiplexer_1_out9), .Q(register_10_q), .clk(clock_1_out));  // open: clr
  Register #(.width(32)) register_11 (
    .D(regval), .en(demultiplexer_1_out10), .Q(register_11_q), .clk(clock_1_out));  // open: clr
  Register #(.width(32)) register_12 (
    .D(regval), .en(demultiplexer_1_out11), .Q(register_12_q), .clk(clock_1_out));  // open: clr
  Register #(.width(32)) register_13 (
    .D(regval), .en(demultiplexer_1_out12), .Q(register_13_q), .clk(clock_1_out));  // open: clr
  Register #(.width(32)) register_14 (
    .D(regval), .en(demultiplexer_1_out13), .Q(register_14_q), .clk(clock_1_out));  // open: clr
  Register #(.width(32)) register_15 (
    .D(regval), .en(demultiplexer_1_out14), .Q(register_15_q), .clk(clock_1_out));  // open: clr
  Register #(.width(32)) register_16 (
    .D(regval), .en(demultiplexer_1_out15), .Q(register_16_q), .clk(clock_1_out));  // open: clr
  Clock clock_1 (.out(clock_1_out));
  Register #(.width(32)) register_17 (
    .D(regval), .en(demultiplexer_1_out16), .Q(register_17_q), .clk(clock_1_out));  // open: clr
  Register #(.width(32)) register_18 (
    .D(regval), .en(demultiplexer_1_out17), .Q(register_18_q), .clk(clock_1_out));  // open: clr
  Register #(.width(32)) register_19 (
    .D(regval), .en(demultiplexer_1_out18), .Q(register_19_q), .clk(clock_1_out));  // open: clr
  Register #(.width(32)) register_20 (
    .D(regval), .en(demultiplexer_1_out19), .Q(register_20_q), .clk(clock_1_out));  // open: clr
  Register #(.width(32)) register_21 (
    .D(regval), .en(demultiplexer_1_out20), .Q(register_21_q), .clk(clock_1_out));  // open: clr
  Register #(.width(32)) register_22 (
    .D(regval), .en(demultiplexer_1_out21), .Q(register_22_q), .clk(clock_1_out));  // open: clr
  Register #(.width(32)) register_23 (
    .D(regval), .en(demultiplexer_1_out22), .Q(register_23_q), .clk(clock_1_out));  // open: clr
  Register #(.width(32)) register_24 (
    .D(regval), .en(demultiplexer_1_out23), .Q(register_24_q), .clk(clock_1_out));  // open: clr
  Register #(.width(32)) register_25 (
    .D(regval), .en(demultiplexer_1_out24), .Q(register_25_q), .clk(clock_1_out));  // open: clr
  Register #(.width(32)) register_26 (
    .D(regval), .en(demultiplexer_1_out25), .Q(register_26_q), .clk(clock_1_out));  // open: clr
  Register #(.width(32)) register_27 (
    .D(regval), .en(demultiplexer_1_out26), .Q(register_27_q), .clk(clock_1_out));  // open: clr
  Register #(.width(32)) register_28 (
    .D(regval), .en(demultiplexer_1_out27), .Q(register_28_q), .clk(clock_1_out));  // open: clr
  Register #(.width(32)) register_29 (
    .D(regval), .en(demultiplexer_1_out28), .Q(register_29_q), .clk(clock_1_out));  // open: clr
  Register #(.width(32)) register_30 (
    .D(regval), .en(demultiplexer_1_out29), .Q(register_30_q), .clk(clock_1_out));  // open: clr
  Register #(.width(32)) register_31 (
    .D(regval), .en(demultiplexer_1_out30), .Q(register_31_q), .clk(clock_1_out));  // open: clr
  Register #(.width(32)) register_32 (
    .D(regval), .en(demultiplexer_1_out31), .Q(register_32_q), .clk(clock_1_out));  // open: clr
  Multiplexer #(.select(5), .width(32)) multiplexer_1 (
    .in0(register_1_q), .in1(register_2_q), .in2(register_3_q), .in3(register_4_q), .in4(register_5_q),
    .in5(register_6_q), .in6(register_7_q), .in7(register_8_q), .in8(register_9_q), .in9(register_10_q),
    .in10(register_11_q), .in11(register_12_q), .in12(register_13_q), .in13(register_14_q),
    .in14(register_15_q), .in15(register_16_q), .in16(register_17_q), .in17(register_18_q),
    .in18(register_19_q), .in19(register_20_q), .in20(register_21_q), .in21(register_22_q),
    .in22(register_23_q), .in23(register_24_q), .in24(register_25_q), .in25(register_26_q),
    .in26(register_27_q), .in27(register_28_q), .in28(register_29_q), .in29(register_30_q),
    .in30(register_31_q), .in31(register_32_q), .out(dreg), .sel(dsel));  // open: en
  Multiplexer #(.select(5), .width(32)) multiplexer_2 (
    .in0(register_1_q), .in1(register_2_q), .in2(register_3_q), .in3(register_4_q), .in4(register_5_q),
    .in5(register_6_q), .in6(register_7_q), .in7(register_8_q), .in8(register_9_q), .in9(register_10_q),
    .in10(register_11_q), .in11(register_12_q), .in12(register_13_q), .in13(register_14_q),
    .in14(register_15_q), .in15(register_16_q), .in16(register_17_q), .in17(register_18_q),
    .in18(register_19_q), .in19(register_20_q), .in20(register_21_q), .in21(register_22_q),
    .in22(register_23_q), .in23(register_24_q), .in24(register_25_q), .in25(register_26_q),
    .in26(register_27_q), .in27(register_28_q), .in28(register_29_q), .in29(register_30_q),
    .in30(register_31_q), .in31(register_32_q), .out(sreg), .sel(ssel));  // open: en
  Multiplexer #(.select(5), .width(32)) multiplexer_3 (
    .in0(register_1_q), .in1(register_2_q), .in2(register_3_q), .in3(register_4_q), .in4(register_5_q),
    .in5(register_6_q), .in6(register_7_q), .in7(register_8_q), .in8(register_9_q), .in9(register_10_q),
    .in10(register_11_q), .in11(register_12_q), .in12(register_13_q), .in13(register_14_q),
    .in14(register_15_q), .in15(register_16_q), .in16(register_17_q), .in17(register_18_q),
    .in18(register_19_q), .in19(register_20_q), .in20(register_21_q), .in21(register_22_q),
    .in22(register_23_q), .in23(register_24_q), .in24(register_25_q), .in25(register_26_q),
    .in26(register_27_q), .in27(register_28_q), .in28(register_29_q), .in29(register_30_q),
    .in30(register_31_q), .in31(register_32_q), .out(treg), .sel(tsel));  // open: en
  // Probe on register_1_q
  // Probe on register_2_q
  // Probe on register_3_q
  // Probe on register_4_q
  // Probe on register_5_q
  // Probe on register_6_q
  // Probe on register_7_q
  // Probe on register_8_q
  // Probe on register_9_q
  // Probe on register_10_q
  // Probe on register_11_q
  // Probe on register_12_q
  // Probe on register_13_q
  // Probe on register_14_q
  // Probe on register_15_q
  // Probe on register_16_q
  // Probe on register_17_q
  // Probe on register_18_q
  // Probe on register_19_q
  // Probe on register_20_q
  // Probe on register_21_q
  // Probe on register_22_q
  // Probe on register_23_q
  // Probe on register_24_q
  // Probe on register_25_q
  // Probe on register_26_q
  // Probe on register_27_q
  // Probe on register_28_q
  // Probe on register_29_q
  // Probe on register_30_q
  // Probe on register_31_q
  // Probe on register_32_q

  // Notes on the sheet:
  //   Register File
endmodule

module ALU (
  input  [31:0] A,
  input  [31:0] B,
  input  [3:0] aluop,
  output Carry,
  output Zero,
  output Negative,
  output [31:0] Result
);

  wire adder_1_cout, or_2_out, subtractor_1_bout;
  wire [31:0] adder_1_out, and_1_out, divider_1_out, divider_1_rem, multiplier_1_out, nand_1_out, nor_1_out,
       not_1_out, or_1_out, shifter_1_out, shifter_2_out, shifter_3_out, shifter_4_out, shifter_5_out,
       subtractor_1_out, xor_1_out;

  assign and_1_out = A & B;  // AND_Gate and_1, 32 bits wide
  assign or_1_out = A | B;  // OR_Gate or_1, 32 bits wide
  assign not_1_out = ~A;  // NOT_Gate not_1, 32 bits wide
  Adder #(.width(32)) adder_1 (.a(A), .b(B), .out(adder_1_out), .cin(1'b0), .cout(adder_1_cout));
  Subtractor #(.width(32)) subtractor_1 (.a(A), .b(B), .out(subtractor_1_out), .bin(1'b0), .bout(subtractor_1_bout));
  Multiplier #(.width(32)) multiplier_1 (.a(A), .b(B), .out(multiplier_1_out), .cin({32{1'b0}}));  // open: cout
  Divider #(.width(32)) divider_1 (.a(A), .b(B), .out(divider_1_out), .upper({32{1'b0}}), .rem(divider_1_rem));
  assign xor_1_out = A ^ B;  // XOR_Gate xor_1, 32 bits wide
  assign nand_1_out = ~(A & B);  // NAND_Gate nand_1, 32 bits wide
  assign nor_1_out = ~(A | B);  // NOR_Gate nor_1, 32 bits wide
  Shifter #(.width(32)) shifter_1 (.in(A), .\dist (B[4:0]), .out(shifter_1_out));
  Shifter #(.width(32), .shift("lr")) shifter_2 (.in(A), .\dist (B[4:0]), .out(shifter_2_out));
  Shifter #(.width(32), .shift("ar")) shifter_3 (.in(A), .\dist (B[4:0]), .out(shifter_3_out));
  Shifter #(.width(32), .shift("rl")) shifter_4 (.in(A), .\dist (B[4:0]), .out(shifter_4_out));
  Shifter #(.width(32), .shift("rr")) shifter_5 (.in(A), .\dist (B[4:0]), .out(shifter_5_out));
  Multiplexer #(.select(4), .width(32), .enable("false")) multiplexer_1 (
    .in0(adder_1_out), .in1(subtractor_1_out), .in2(multiplier_1_out), .in3(divider_1_out),
    .in4(divider_1_rem), .in5(and_1_out), .in6(or_1_out), .in7(xor_1_out), .in8(nand_1_out), .in9(nor_1_out),
    .in10(not_1_out), .in11(shifter_1_out), .in12(shifter_2_out), .in13(shifter_3_out), .in14(shifter_4_out),
    .in15(shifter_5_out), .out({Negative, Result[30:0]}), .sel(aluop));
  Multiplexer #(.select(4), .enable("false")) multiplexer_2 (
    .in0(adder_1_cout), .in1(subtractor_1_bout), .in2(1'b0), .in3(1'b0), .in4(1'b0), .in5(1'b0), .in6(1'b0),
    .in7(1'b0), .in8(1'b0), .in9(1'b0), .in10(1'b0), .in11(1'b0), .in12(1'b0), .in13(1'b0), .in14(1'b0),
    .in15(1'b0), .out(Carry), .sel(aluop));
  or or_2 (or_2_out, Result[0], Result[1], Result[2], Result[3], Result[4], Result[5], Result[6], Result[7], Result[8], Result[9], Result[10], Result[11], Result[12], Result[13], Result[14], Result[15], Result[17], Result[18], Result[19], Result[20], Result[21], Result[22], Result[23], Result[24], Result[25], Result[26], Result[27], Result[28], Result[29], Result[30], Negative, Result[16]);
  not not_2 (Zero, or_2_out);

  assign Result[31] = Negative;

  // Notes on the sheet:
  //   32-bit ALU
endmodule

// PC
module pclogic (
  input  [31:0] imreg,
  input  pcload,
  input  reset,
  input  [1:0] pcsel,
  input  [31:0] sreg,
  output [31:0] pcout
);

  wire clock_1_out;
  wire [31:0] adder_1_out, adder_2_out, multiplexer_1_out;

  Adder #(.width(32)) adder_1 (.a(pcout), .b(32'h1), .out(adder_1_out));  // open: cin, cout
  Adder #(.width(32)) adder_2 (.a(pcout), .b(imreg), .out(adder_2_out));  // open: cin, cout
  Multiplexer #(.select(2), .width(32), .enable("false")) multiplexer_1 (
    .in0(adder_1_out), .in1(imreg), .in2(adder_2_out), .in3(sreg), .out(multiplexer_1_out), .sel(pcsel));
  Register #(.width(32)) PC (.D(multiplexer_1_out), .en(pcload), .Q(pcout), .clk(clock_1_out), .clr(reset));
  Clock clock_1 (.out(clock_1_out));

  // Notes on the sheet:
  //   PC Logic
endmodule

module ucodelogic (
  input  z,
  input  n,
  input  c,
  input  [6:0] opcode,
  output [3:0] aluop,
  output [1:0] op2sel,
  output datawrite,
  output [7:0] ucounter,
  output [1:0] addrsel,
  output [1:0] pcsel,
  output pcload,
  output dwrite,
  output irload,
  output imload,
  output [1:0] regsrc,
  output [1:0] datasel,
  output swrite
);

  wire clock_1_out, indexsel, multiplexer_2_out, or_1_out;
  wire [1:0] cond;
  wire [7:0] adder_1_out, multiplexer_1_out, multiplexer_3_out;
  wire [15:0] rom_2_data;
  wire [31:23] rom_1_data;

  Register Microcounter (.D(adder_1_out), .Q(ucounter), .clk(clock_1_out));  // open: en, clr
  Clock clock_1 (.out(clock_1_out));
  ROM #(.dataWidth(32)) rom_1 (
    .addr(ucounter),
    .data({rom_1_data, swrite, datasel, indexsel, cond, regsrc, imload, irload, dwrite, pcload, pcsel, addrsel, datawrite, op2sel, aluop}));  // open: sel
  ROM #(.dataWidth(16)) rom_2 (.addr(ucounter), .data(rom_2_data));  // open: sel
  or or_1 (or_1_out, z, n);
  Multiplexer #(.width(8), .enable("false")) multiplexer_1 (
    .in0(rom_2_data[7:0]), .in1(rom_2_data[15:8]), .out(multiplexer_1_out), .sel(multiplexer_2_out));
  Multiplexer #(.select(2), .enable("false")) multiplexer_2 (
    .in0(z), .in1(or_1_out), .in2(n), .in3(c), .out(multiplexer_2_out), .sel(cond));
  Multiplexer #(.width(8), .enable("false")) multiplexer_3 (
    .in0({8{1'b0}}), .in1({1'b0, opcode}), .out(multiplexer_3_out), .sel(indexsel));
  Adder adder_1 (.a(multiplexer_1_out), .b(multiplexer_3_out), .out(adder_1_out));  // open: cin, cout

  // Notes on the sheet:
  //   Control ROM
  //   contents of rom_1 (hex, n*v repeats v):
  //   2000 80800 11000 11001 11002 11003 36*0 4000 22*0 1000 0 4000 62*0 21 800 1000c0 800 800 a00
  //   Decision ROM
  //   contents of rom_2 (hex, n*v repeats v):
  //   101 202 40*0 8282 22*0 8383 0 8484 62*0 8687 0 8585
endmodule
